# Fritzing sketch WALL-E (saved by Fritzing 0.9.3b)

parts:
  S1 = H-Bridge with L298N
  Raspberry_Pi_1 = Raspberry Pi 3 [part_number=RPI-3-V1.2]
  Part1 = Mono 2.5W Class D Audio Amplifier - PAM8302
  M1 = RioRand LM2596
  M2 = RioRand LM2596
  U1 = LIPO-2000mAh [package=lipo-2000]
  PWM1 = PCA9685 16x12-bit PWM Breakout
  Part2 = Adafruit ADS1115 16Bit I2C ADC [part_number="Adafruit #1085"]
  J2 = Basic Servo
  U2 = TRANSCHIPTC5747 [package=camera_sfv24r-2st_2]  # not connected
  SPKR1 = Loudspeaker
  J3 = Infrared Proximity Sensor
  J4 = Basic Servo
  J7 = Basic Servo
  J11 = Basic Servo
  J12 = Basic Servo
  J13 = Basic Servo
  J14 = Camdenboss CTB0158-10 [part_number=CTB0158-10 package=THT]
  J10 = Camdenboss CTB0158-10 [part_number=CTB0158-10 package=THT]

nets:
  N1: S1.12V, M1.Pin_3
  N2: S1.GND, J14.pin4
  N3: S1.5V, J10.pin3
  N4: S1.ENA, PWM1.no_name_yet#0
  N5: S1.IN1, PWM1.no_name_yet#1
  N6: S1.IN2, PWM1.no_name_yet#2
  N7: S1.IN3, PWM1.no_name_yet#4
  N8: S1.IN4, PWM1.no_name_yet#3
  N9: S1.ENB, PWM1.no_name_yet#5
  N10: S1.M1-01, J4.vcc
  N11: S1.M1-02, J4.gnd
  N12: S1.M2-01, J2.gnd
  N13: S1.M2-02, J2.vcc
  N14: Raspberry_Pi_1.3v3, Raspberry_Pi_1.GPIO2, PWM1.no_name_yet#504, PWM1.no_name_yet#604, Part2.SDA
  GND: Raspberry_Pi_1.GPIO3, Raspberry_Pi_1.GPIO4, Raspberry_Pi_1.GND, PWM1.no_name_yet#501, PWM1.no_name_yet#503, PWM1.no_name_yet#601, PWM1.no_name_yet#603, PWM1.no_name_yet#701, PWM1.no_name_yet#1006, PWM1.no_name_yet#1007, PWM1.no_name_yet#1008, PWM1.no_name_yet#1009, Part2.SCL, Part2.GND, J7.gnd, J11.gnd, J12.gnd, J13.gnd, J14.pin5, J14.pin6
  5V: Raspberry_Pi_1.5V, PWM1.no_name_yet#505, PWM1.no_name_yet#605, Part2.VDD, J10.pin4
  N15: Part1.GND, J14.pin3
  N16: Part1.VCC, Part1.SD, J10.pin2
  N17: Part1.VO+, SPKR1.pin1
  N18: Part1.VO-, SPKR1.pin2
  N19: M1.Pin_1, M2.Pin_1, U1.+
  N20: M1.Pin_2, M2.Pin_2, U1.-
  N21: M1.Pin_4, J14.pin2
  N22: M2.Pin_3, J10.pin1
  N23: M2.Pin_4, J14.pin1
  N24: PWM1.no_name_yet#6, J7.pulse
  N25: PWM1.no_name_yet#7, J11.pulse
  N26: PWM1.no_name_yet#8, J12.pulse
  N27: PWM1.no_name_yet#9, J13.pulse
  VCC: PWM1.no_name_yet#106, PWM1.no_name_yet#107, PWM1.no_name_yet#108, PWM1.no_name_yet#109, PWM1.no_name_yet#706, J7.vcc, J11.vcc, J12.vcc, J13.vcc, J10.pin5
  N28: Part2.AIN0, Part2.ALERT, J3.Vout
  N29: J3.GND, J14.pin7
  N30: J3.Vcc, J10.pin6

notes:
  5V
  12V
  GND
  Camera
  Audio Amplifier
  Speaker
  Raspberry Pi
  Arm
  left
  Arm
  right
  Head
  up/down
  Head
  left/right
  IR obstacle sensor
  AD converter
  Track
  left
  Track
  right
  DC motor
  H-bridge
  Servo driver
  Lipo battery
  DC/DC converter

custom parts:
  H-Bridge with L298N: h-bridge
  Mono 2.5W Class D Audio Amplifier - PAM8302: A super small but powerful mono amplifier able to deliver up to 2.5 Watts into 4-8 ohm impedance speakers. Inside the miniature chip is a class D controller, able to run from 2.0V-5.5VDC. Since the amp is a class D, its very efficient (over 90% efficient when driving an 8Ω speaker at over half a Watt) - making it perfect for portable and battery-powered projects.
  Adafruit ADS1115 16Bit I2C ADC: For microcontrollers without an analog-to-digital converter or when you want a higher-precision ADC, the ADS1115 provides 16-bit precision at 860 samples/second over I2C. The chip can be configured as 4 single-ended input channels, or two differential channels. As a nice bonus, it even includes a programmable gain amplifier, up to x16, to help boost up smaller single/differential signals to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
